# Fritzing sketch diagram (saved by Fritzing 1.0.2b)

parts:
  esp1 = ESP32 DevKitc V4
  U1 = RJ45 Jack [package=rj45-8]
  Part1 = LCD1602-I2C
  U2 = LIPO-2000mAh [package=lipo-2000]

nets:
  N1: esp1.IO21, Part1.SDA
  N2: esp1.IO22, Part1.SCL
  N3: esp1.GND#18, Part1.GND
  N4: esp1.3V3, U2.+
  N5: esp1.IO34, U1.6
  N6: esp1.IO35, U1.5
  N7: esp1.GND#32, U1.3, U1.4, U2.-
  5V: esp1.5V, U1.1, Part1.VCC

custom parts:
  ESP32 DevKitc V4: ESP32-DevKitC board with ESP32-WROOM-32 module. ESP32-DevKitC V4 is a small-sized ESP32-based development board produced by Espressif. Most of the pins on the ESP module are broken out to the pin headers on the board. The pins D0, D1, D2, D3, CMD and CLK are used internally for communication between ESP32 and SPI flash memory. They are grouped on both sides near the USB connector. Avoid using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
  LCD1602-I2C: A standard character display, usually with 2x16 characters. Comes in many colors with LCM1602 IIC attached.
